# Fritzing sketch pico_wiz850io_neopixel (saved by Fritzing 0.9.3b)

parts:
  Mod1 = Raspberry Pi Pico
  WIZ820io1 = WIZ820io [part_number=WIZ820io]
  NEOPIXEL2 = Neopixel Strip -- Black (30/m)

nets:
  N1: Mod1.pin_5, NEOPIXEL2.DI
  GND: Mod1.pin_13, Mod1.pin_14, Mod1.pin_23, Mod1.pin_38, WIZ820io1.GND, WIZ820io1.SCLK, NEOPIXEL2.GND
  N2: Mod1.pin_15, WIZ820io1.MOSI
  N3: Mod1.pin_16, WIZ820io1.MISO
  N4: Mod1.pin_17, WIZ820io1.nSS
  N5: Mod1.pin_20, WIZ820io1.nRESET
  N6: Mod1.pin_36, WIZ820io1.VIN
  N7: Mod1.pin_40, NEOPIXEL2.+5V

custom parts:
  Raspberry Pi Pico: Raspberry Pi Pico. Based around the RP2040 microcontroller the Pico is a low cost microcontroller device bringing Raspberry Pi quality, cost, and easy of use to the microcontroller space. Jan 2021, Split part in to two versions: tht (this one) and SMD. This one will drill holes for a .1 in header in pcb to allow plugging in the module as well as providing pads to solder the module to the top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
  Neopixel Strip -- Black (30/m): Neopixel Strip, Black, 30 pixels per meter.
